# Fritzing sketch control-panel-2-wiring (saved by Fritzing 0.9.3b)
breadboards: 1

parts:
  WeMos_D1_Mini1 = WeMos D1 Mini
  U1 = SWITCH-SPST-2 [package=switch-spst-vertical]
  U2 = SWITCH-SPST-2 [package=switch-spst-vertical]
  U3 = SWITCH-SPST-2 [package=switch-spst-vertical]
  LED1 = LED - 5mm [color="White (6500K)" package="5 mm [THT]"]
  LED2 = LED - 5mm [color="White (4500K)" package="5 mm [THT]"]
  LED3 = LED - 5mm [color="White (4500K)" package="5 mm [THT]"]
  LED4 = LED - 5mm [color="White (4500K)" package="5 mm [THT]"]
  LED5 = LED - 5mm [color="Green (565nm)" package="5 mm [THT]"]
  R1 = Resistor [tolerance=±5% resistance=200 package=THT]
  R2 = Resistor [tolerance=±5% resistance=200 package=THT]
  R3 = Resistor [tolerance=±5% resistance=200 package=THT]
  R4 = Resistor [tolerance=±5% resistance=200 package=THT]
  R5 = Resistor [tolerance=±5% resistance=200 package=THT]
  R6 = Resistor [tolerance=±5% resistance=10k package=THT]
  R7 = Resistor [tolerance=±5% resistance=10k package=THT]
  R8 = Resistor [tolerance=±5% resistance=10k package=THT]

nets:
  N1: WeMos_D1_Mini1.3V3, U1.O, U2.O, U3.O, LED1.anode
  N2: WeMos_D1_Mini1.D0, U1.P, LED2.anode, R7.Pin_0
  N3: WeMos_D1_Mini1.D1, U2.P, LED4.anode, R6.Pin_0
  N4: WeMos_D1_Mini1.D2, U3.P, LED3.anode, R8.Pin_0
  N5: WeMos_D1_Mini1.D7, LED5.anode
  N6: WeMos_D1_Mini1.G, R1.Pin_0, R2.Pin_0, R3.Pin_1, R4.Pin_1, R5.Pin_1, R6.Pin_1, R7.Pin_1, R8.Pin_1
  N7: LED1.cathode, R1.Pin_1
  N8: LED2.cathode, R3.Pin_0
  N9: LED3.cathode, R4.Pin_0
  N10: LED4.cathode, R5.Pin_0
  N11: LED5.cathode, R2.Pin_1
