# Fritzing sketch control-panel-3-wiring (saved by Fritzing 0.9.3b)
breadboards: 1

parts:
  U1 = NodeMCU V1.0
  LED1 = LED - 5mm [color="White (4500K)" package="5 mm [THT]"]
  R1 = Resistor [tolerance=±5% resistance=100 package=THT]
  LED2 = LED - 5mm [color="White (8000K)" package="5 mm [THT]"]
  LED3 = LED - 5mm [color="Red (635nm)" package="5 mm [THT]"]
  IR1 = TSOP312.., 314.. [package=THT]
  R2 = Resistor [tolerance=±5% resistance=100 package=THT]
  R3 = Resistor [tolerance=±5% resistance=100 package=THT]

nets:
  N1: U1.D1, LED3.anode
  N2: U1.D2, IR1.Data
  N3: U1.3V3, LED1.anode, R1.Pin_1, IR1.Vs, R2.Pin_1, R3.Pin_1
  GND: U1.GND, IR1.GND
  N4: U1.D5, LED2.anode
  N5: LED1.cathode, R1.Pin_0
  N6: LED2.cathode, R2.Pin_0
  N7: LED3.cathode, R3.Pin_0

custom parts:
  NodeMCU V1.0: ESP8266 based NodeMCU
