# Fritzing sketch wiring (saved by Fritzing 0.9.3b)
breadboards: 1

parts:
  J1 = Piezo Speaker
  S1 = Pushbutton [package="[THT]"]
  S2 = Pushbutton [package="[THT]"]
  Part1 = Adafruit OLED FeatherWing [part_number="Adafruit #2900"]
  Part2 = Adafruit Feather 32u4 Basic Proto [part_number="Adafruit #2771"]

nets:
  GND: J1.pin1, S1.Pin_1, S1.Pin_2, S2.Pin_1, S2.Pin_2, Part1.GND, Part1.G, Part2.GND
  N1: J1.pin2, Part1.L, Part2.11
  N2: S1.Pin_3, S1.Pin_4, Part1.I, Part2.6
  N3: S2.Pin_3, S2.Pin_4, Part1.H, Part2.5
  N4: Part1.!RESET, Part2.RST
  3.3V: Part1.3.3V, Part2.+3V3
  N5: Part1.AREF, Part2.AREF
  N6: Part1.A, Part2.A0
  N7: Part1.B, Part2.A1
  N8: Part1.C, Part2.A2
  N9: Part1.D, Part2.A3
  N10: Part1.E, Part2.A4
  N11: Part1.F, Part2.A5
  N12: Part1.SCK, Part2.SCK
  N13: Part1.MOSI, Part2.MOSI
  N14: Part1.MISO, Part2.MISO
  N15: Part1.RX, Part2.0
  N16: Part1.TX, Part2.1
  N17: Part1.SDA, Part2.2
  N18: Part1.SCL, Part2.3
  N19: Part1.J, Part2.9
  N20: Part1.K, Part2.10
  N21: Part1.M, Part2.12
  N22: Part1.N, Part2.13
  N23: Part1.USB, Part2.VBUS
  N24: Part1.EN, Part2.EN
  N25: Part1.VBAT, Part2.VBAT

custom parts:
  Adafruit OLED FeatherWing: This is the FeatherWing OLED: it adds a 128x32 monochrome OLED plus 3 user buttons to any Feather main board. These displays are small, only about 1" diagonal, but very readable due to the high contrast of an OLED display. This screen is made of 128x32 individual white OLED pixels and because the display makes its own light, no backlight is required. This reduces the power required to run the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
  Adafruit Feather 32u4 Basic Proto: At the Feather 32u4's heart is at ATmega32u4 clocked at 8 MHz and at 3.3V logic, a chip setup we've had tons of experience with as it's the same as the Flora. This chip has 32K of flash and 2K of RAM, with built in USB so not only does it have a USB-to-Serial program & debug capability built in with no need for an FTDI-like chip, it can also act like a mouse, keyboard, USB MIDI device, etc.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
