# Fritzing sketch power-relay-wiring (saved by Fritzing 0.9.3b)
breadboards: 1

parts:
  OMRON1 = OMRON PCB Power Relay – G5LE [part_number="G5LE-1\n" package=THT]
  Q1 = NPN-Transistor [package="TO92 [THT]"]
  D1 = Rectifier Diode [part_number=1N4148 package="300 mil [THT]"]
  R1 = Resistor [tolerance=±5% resistance=10k package=THT]
  R2 = Resistor [tolerance=±5% resistance=1k package=THT]
  R3 = Resistor [tolerance=±5% resistance=120 package=THT]
  LED1 = LED - 5mm [color="Green (555nm)" package="5 mm [THT]"]
  J2 = screw terminal, 3 pins
  J3 = screw terminal, 3 pins

nets:
  N1: OMRON1.A, J3.pin3
  N2: OMRON1.COIL1, Q1.C, D1.anode, R3.Pin_1
  N3: OMRON1.C, J3.pin2
  N4: OMRON1.COIL2, D1.cathode, LED1.anode, J2.pin3
  N5: OMRON1.B, J3.pin1
  N6: Q1.E, R1.Pin_0, J2.pin2
  N7: Q1.B, R1.Pin_1, R2.Pin_1
  N8: R2.Pin_0, J2.pin1
  N9: R3.Pin_0, LED1.cathode

notes:
  In, GND, 5v
  NO, HIGH Voltage, NC
